# Fritzing sketch motor_controller_mosfet_soft_start_attiny85 (saved by Fritzing 0.9.9b)
breadboards: 2

parts:
  IC1 = IC, DIP package, 8 pins [chip_label=ATtiny]
  Q1 = Basic FET P-Channel [package="TO220 [THT]"]
  R1 = Resistor [tolerance=±5% power=0.25 resistance=10k package=THT]
  LED1 = LED - 5mm [color="Red (633nm)" current=0.030 package="5 mm [THT]"]
  R2 = Resistor [tolerance=±5% power=0.25 resistance=220 package=THT]
  S1 = Pushbutton [package="[THT]"]
  D1 = Rectifier Diode [part_number=1N4001 package="300 mil [THT]"]
  L1 = Solenoid
  R4 = Trimmer Potentiometer [maximum_resistance=10kΩ package=THT]
  Part1 = DC Voltage Source 5V [package=THT]
  Part2 = DC Voltage Source 12V [package=THT]

nets:
  N1: IC1.pin3, R4.wiper
  N2: IC1.pin4, IC1.pin7, Q1.source, R1.Pin_0, R2.Pin_0, S1.Pin_1, S1.Pin_2, S1.Pin_3, S1.Pin_4, R4.leg1, Part1.V–, Part2.V–
  N3: IC1.pin5, LED1.cathode
  N4: IC1.pin6, Q1.gate, R1.Pin_1
  N5: IC1.pin8, R4.leg2, Part1.V+
  N6: Q1.drain, D1.anode, L1.pin1
  N7: LED1.anode, R2.Pin_1
  N8: D1.cathode, L1.pin2, Part2.V+

custom parts:
  DC Voltage Source 5V: A dummy, proxy, ersatz, stand-in part for whatever you want. With 3 pins on a 100 mil inline pin header footprint.
