# Fritzing sketch motor_controller_mosfet_soft_start_uno (saved by Fritzing 0.9.9b)
breadboards: 1

parts:
  Part1 = Arduino Uno (Rev3)
  Q1 = Basic FET P-Channel [package="TO220 [THT]"]
  R1 = Resistor [tolerance=±5% power=0.25 resistance=10k package=THT]
  LED1 = LED - 5mm [color="Red (633nm)" current=0.030 package="5 mm [THT]"]
  R2 = Resistor [tolerance=±5% power=0.25 resistance=220 package=THT]
  S1 = Pushbutton [package="[THT]"]
  D1 = Rectifier Diode [part_number=1N4001 package="300 mil [THT]"]
  L1 = Solenoid
  R4 = Trimmer Potentiometer [maximum_resistance=10kΩ package=THT]
  Part2 = DC Voltage Source 12V

nets (from the breadboard view):
  N1: Part1.A0, R4.wiper
  N2: Part1.D2, Part1.GND, Q1.source, R1.Pin_0, R2.Pin_0, S1.Pin_1, S1.Pin_2, S1.Pin_3, S1.Pin_4, R4.leg1, Part2.connector3
  N3: Part1.D3_PWM, Q1.gate, R1.Pin_1
  N4: Part1.D4, LED1.cathode
  N5: Part1.5V, R4.leg2
  N6: Q1.drain, D1.anode, L1.pin1
  N7: LED1.anode, R2.Pin_1
  N8: D1.cathode, L1.pin2, Part2.connector2
